// Logisim project 16 bit register + register file.circ as structural Verilog
module _16_bit_register (
  input  C,
  input  write,
  input  reset,
  input  [15:0] D,
  output [15:0] Q
);

  D_Flip_Flop #(.trigger("falling")) d_ff_1 (
    .clk(C), .D(D[0]), .Q(Q[0]), .en(write), .reset(reset));  // open: Qn, preset
  D_Flip_Flop #(.trigger("falling")) d_ff_2 (
    .clk(C), .D(D[1]), .Q(Q[1]), .en(write), .reset(reset));  // open: Qn, preset
  D_Flip_Flop #(.trigger("falling")) d_ff_3 (
    .clk(C), .D(D[2]), .Q(Q[2]), .en(write), .reset(reset));  // open: Qn, preset
  D_Flip_Flop #(.trigger("falling")) d_ff_4 (
    .clk(C), .D(D[3]), .Q(Q[3]), .en(write), .reset(reset));  // open: Qn, preset
  D_Flip_Flop #(.trigger("falling")) d_ff_5 (
    .clk(C), .D(D[4]), .Q(Q[4]), .en(write), .reset(reset));  // open: Qn, preset
  D_Flip_Flop #(.trigger("falling")) d_ff_6 (
    .clk(C), .D(D[5]), .Q(Q[5]), .en(write), .reset(reset));  // open: Qn, preset
  D_Flip_Flop #(.trigger("falling")) d_ff_7 (
    .clk(C), .D(D[6]), .Q(Q[6]), .en(write), .reset(reset));  // open: Qn, preset
  D_Flip_Flop #(.trigger("falling")) d_ff_8 (
    .clk(C), .D(D[7]), .Q(Q[7]), .en(write), .reset(reset));  // open: Qn, preset
  D_Flip_Flop #(.trigger("falling")) d_ff_9 (
    .clk(C), .D(D[8]), .Q(Q[8]), .en(write), .reset(reset));  // open: Qn, preset
  D_Flip_Flop #(.trigger("falling")) d_ff_10 (
    .clk(C), .D(D[9]), .Q(Q[9]), .en(write), .reset(reset));  // open: Qn, preset
  D_Flip_Flop #(.trigger("falling")) d_ff_11 (
    .clk(C), .D(D[10]), .Q(Q[10]), .en(write), .reset(reset));  // open: Qn, preset
  D_Flip_Flop #(.trigger("falling")) d_ff_12 (
    .clk(C), .D(D[11]), .Q(Q[11]), .en(write), .reset(reset));  // open: Qn, preset
  D_Flip_Flop #(.trigger("falling")) d_ff_13 (
    .clk(C), .D(D[12]), .Q(Q[12]), .en(write), .reset(reset));  // open: Qn, preset
  D_Flip_Flop #(.trigger("falling")) d_ff_14 (
    .clk(C), .D(D[13]), .Q(Q[13]), .en(write), .reset(reset));  // open: Qn, preset
  D_Flip_Flop #(.trigger("falling")) d_ff_15 (
    .clk(C), .D(D[14]), .Q(Q[14]), .en(write), .reset(reset));  // open: Qn, preset
  D_Flip_Flop #(.trigger("falling")) d_ff_16 (
    .clk(C), .D(D[15]), .Q(Q[15]), .en(write), .reset(reset));  // open: Qn, preset
endmodule

module register_file (
  input  [3:0] rd,
  input  Write,
  input  R,
  input  [3:0] rs,
  input  C,
  input  [15:0] DATA,
  input  [3:0] rt,
  output [15:0] S,
  output [15:0] T,
  output [15:0] G0,
  output [15:0] G1,
  output [15:0] G2,
  output [15:0] G3,
  output [15:0] G4,
  output [15:0] G5,
  output [15:0] G6,
  output [15:0] G7,
  output [15:0] G8,
  output [15:0] G9,
  output [15:0] G10,
  output [15:0] G11,
  output [15:0] G12,
  output [15:0] G13,
  output [15:0] G14,
  output [15:0] G15
);

  wire demultiplexer_1_out0, demultiplexer_1_out1, demultiplexer_1_out2, demultiplexer_1_out3,
       demultiplexer_1_out4, demultiplexer_1_out5, demultiplexer_1_out6, demultiplexer_1_out7,
       demultiplexer_1_out8, demultiplexer_1_out9, demultiplexer_1_out10, demultiplexer_1_out11,
       demultiplexer_1_out12, demultiplexer_1_out13, demultiplexer_1_out14, demultiplexer_1_out15;

  Demultiplexer #(.select(4), .disabled(0)) demultiplexer_1 (
    .out0(demultiplexer_1_out0), .out1(demultiplexer_1_out1), .out2(demultiplexer_1_out2),
    .out3(demultiplexer_1_out3), .out4(demultiplexer_1_out4), .out5(demultiplexer_1_out5),
    .out6(demultiplexer_1_out6), .out7(demultiplexer_1_out7), .out8(demultiplexer_1_out8),
    .out9(demultiplexer_1_out9), .out10(demultiplexer_1_out10), .out11(demultiplexer_1_out11),
    .out12(demultiplexer_1_out12), .out13(demultiplexer_1_out13), .out14(demultiplexer_1_out14),
    .out15(demultiplexer_1_out15), .in(Write), .sel(rd), .en(C));
  _16_x_16_bit_registers u_16_x_16_bit_registers_1 (
    .R1_D(DATA), .R2_D(DATA), .R3_D(DATA), .R4_D(DATA), .R5_D(DATA), .R6_D(DATA), .R7_D(DATA), .R8_D(DATA),
    .R9_D(DATA), .R10_D(DATA), .R11_D(DATA), .R12_D(DATA), .R13_D(DATA), .R14_D(DATA), .R15_D(DATA),
    .R16_D(DATA), .R1_write(demultiplexer_1_out0), .R2_write(demultiplexer_1_out1),
    .R3_write(demultiplexer_1_out2), .R4_write(demultiplexer_1_out3), .R5_write(demultiplexer_1_out4),
    .R6_write(demultiplexer_1_out5), .R7_write(demultiplexer_1_out6), .R8_write(demultiplexer_1_out7),
    .R9_write(demultiplexer_1_out8), .R10_write(demultiplexer_1_out9), .R11_write(demultiplexer_1_out10),
    .R12_write(demultiplexer_1_out11), .R13_write(demultiplexer_1_out12), .R14_write(demultiplexer_1_out13),
    .R15_write(demultiplexer_1_out14), .R16_write(demultiplexer_1_out15), .Reset(R), .C(C), .R1_Q(G0),
    .R2_Q(G1), .R3_Q(G2), .R4_Q(G3), .R5_Q(G4), .R6_Q(G5), .R7_Q(G6), .R8_Q(G7), .R9_Q(G8), .R10_Q(G9),
    .R11_Q(G10), .R12_Q(G11), .R13_Q(G12), .R14_Q(G13), .R15_Q(G14), .R16_Q(G15));
  Multiplexer #(.select(4), .width(16), .disabled(0)) multiplexer_1 (
    .in0(G0), .in1(G1), .in2(G2), .in3(G3), .in4(G4), .in5(G5), .in6(G6), .in7(G7), .in8(G8), .in9(G9),
    .in10(G10), .in11(G11), .in12(G12), .in13(G13), .in14(G14), .in15(G15), .out(S), .sel(rs), .en(1'b1));
  Multiplexer #(.select(4), .width(16), .disabled(0)) multiplexer_2 (
    .in0(G0), .in1(G1), .in2(G2), .in3(G3), .in4(G4), .in5(G5), .in6(G6), .in7(G7), .in8(G8), .in9(G9),
    .in10(G10), .in11(G11), .in12(G12), .in13(G13), .in14(G14), .in15(G15), .out(T), .sel(rt), .en(1'b1));
endmodule

module _16_x_16_bit_registers (
  input  Reset,
  input  C,
  input  R1_write,
  input  [15:0] R1_D,
  input  R2_write,
  input  [15:0] R2_D,
  input  R3_write,
  input  [15:0] R3_D,
  input  R4_write,
  input  [15:0] R4_D,
  input  R5_write,
  input  [15:0] R5_D,
  input  R6_write,
  input  [15:0] R6_D,
  input  R7_write,
  input  [15:0] R7_D,
  input  R8_write,
  input  [15:0] R8_D,
  input  R9_write,
  input  [15:0] R9_D,
  input  R10_write,
  input  [15:0] R10_D,
  input  R11_write,
  input  [15:0] R11_D,
  input  R12_write,
  input  [15:0] R12_D,
  input  R13_write,
  input  [15:0] R13_D,
  input  R14_write,
  input  [15:0] R14_D,
  input  R15_write,
  input  [15:0] R15_D,
  input  R16_write,
  input  [15:0] R16_D,
  output [15:0] R1_Q,
  output [15:0] R2_Q,
  output [15:0] R3_Q,
  output [15:0] R4_Q,
  output [15:0] R5_Q,
  output [15:0] R6_Q,
  output [15:0] R7_Q,
  output [15:0] R8_Q,
  output [15:0] R9_Q,
  output [15:0] R10_Q,
  output [15:0] R11_Q,
  output [15:0] R12_Q,
  output [15:0] R13_Q,
  output [15:0] R14_Q,
  output [15:0] R15_Q,
  output [15:0] R16_Q
);

  _16_bit_register u_16_bit_register_1 (.D({16{1'b0}}), .C(C), .write(R1_write), .reset(Reset), .Q(R1_Q));
  _16_bit_register u_16_bit_register_2 (.D(R2_D), .C(C), .write(R2_write), .reset(Reset), .Q(R2_Q));
  _16_bit_register u_16_bit_register_3 (.D(R3_D), .C(C), .write(R3_write), .reset(Reset), .Q(R3_Q));
  _16_bit_register u_16_bit_register_4 (.D(R4_D), .C(C), .write(R4_write), .reset(Reset), .Q(R4_Q));
  _16_bit_register u_16_bit_register_5 (.D(R5_D), .C(C), .write(R5_write), .reset(Reset), .Q(R5_Q));
  _16_bit_register u_16_bit_register_6 (.D(R6_D), .C(C), .write(R6_write), .reset(Reset), .Q(R6_Q));
  _16_bit_register u_16_bit_register_7 (.D(R7_D), .C(C), .write(R7_write), .reset(Reset), .Q(R7_Q));
  _16_bit_register u_16_bit_register_8 (.D(R8_D), .C(C), .write(R8_write), .reset(Reset), .Q(R8_Q));
  _16_bit_register u_16_bit_register_9 (.D(R9_D), .C(C), .write(R9_write), .reset(Reset), .Q(R9_Q));
  _16_bit_register u_16_bit_register_10 (.D(R10_D), .C(C), .write(R10_write), .reset(Reset), .Q(R10_Q));
  _16_bit_register u_16_bit_register_11 (.D(R11_D), .C(C), .write(R11_write), .reset(Reset), .Q(R11_Q));
  _16_bit_register u_16_bit_register_12 (.D(R12_D), .C(C), .write(R12_write), .reset(Reset), .Q(R12_Q));
  _16_bit_register u_16_bit_register_13 (.D(R13_D), .C(C), .write(R13_write), .reset(Reset), .Q(R13_Q));
  _16_bit_register u_16_bit_register_14 (.D(R14_D), .C(C), .write(R14_write), .reset(Reset), .Q(R14_Q));
  _16_bit_register u_16_bit_register_15 (.D(R15_D), .C(C), .write(R15_write), .reset(Reset), .Q(R15_Q));
  _16_bit_register u_16_bit_register_16 (.D(R16_D), .C(C), .write(R16_write), .reset(Reset), .Q(R16_Q));
endmodule
