// Logisim project ALU_Group11.circ as structural Verilog: 19 circuits, main circuit main
module main (
  output halt,
  output [8:0] counter,
  output [3:0] op,
  output [15:0] a,
  output [15:0] b,
  output [15:0] oracle,
  output [15:0] result,
  output err_oracle,
  output error,
  output ok,
  output start_delimiter
);

  wire and_1_out, and_2_out, comparator_1_eq, comparator_2_eq;

  Counter #(.width(9), .max('h1ff), .trigger("falling")) counter_1 (
    .Q(counter), .carry(halt));  // open: load, D, count, clk, clr
  RAM #(.addrWidth(12), .dataWidth(4), .bus("separate")) ram_1 (
    .addr({counter, 3'b000}), .data(op), .ld(1'b1));  // open: din, str, sel, clk, clr
  RAM #(.addrWidth(12), .dataWidth(16), .bus("separate")) ram_2 (
    .addr({counter, 3'b001}), .data(a), .ld(1'b1));  // open: din, str, sel, clk, clr
  RAM #(.addrWidth(12), .dataWidth(16), .bus("separate")) ram_3 (
    .addr({counter, 3'b010}), .data(b), .ld(1'b1));  // open: din, str, sel, clk, clr
  RAM #(.addrWidth(12), .dataWidth(16), .bus("separate")) ram_4 (
    .addr({counter, 3'b011}), .data(oracle), .ld(1'b1));  // open: din, str, sel, clk, clr
  RAM #(.addrWidth(12), .dataWidth(1), .bus("separate")) ram_5 (
    .addr({counter, 3'b100}), .data(err_oracle), .ld(1'b1));  // open: din, str, sel, clk, clr
  RAM #(.addrWidth(12), .dataWidth(1), .bus("separate")) ram_6 (
    .addr({counter, 3'b101}), .data(start_delimiter), .ld(1'b1));  // open: din, str, sel, clk, clr
  _16_bit_ALU u_16_bit_alu_1 (.ALU_code(op), .a(a), .b(b), .result(result), .overflow(error));
  Comparator #(.width(1), .mode("unsigned")) comparator_1 (
    .a(error), .b(err_oracle), .eq(comparator_1_eq));  // open: gt, lt
  Comparator #(.width(16)) comparator_2 (.a(result), .b(oracle), .eq(comparator_2_eq));  // open: gt, lt
  and and_1 (and_1_out, comparator_1_eq, error);
  and and_2 (and_2_out, comparator_2_eq, comparator_1_eq, ~error);  // AND_Gate
  or or_1 (ok, and_1_out, and_2_out);

  // Notes on the sheet:
  //   You must complete the circuit '16-bit ALU' instead.
  //   DO NOT EDIT THIS CIRCUIT!
endmodule

module _16_bit_ALU (
  input  [3:0] ALU_code,
  input  [15:0] a,
  input  [15:0] b,
  output [15:0] result,
  output overflow
);

  wire [16:0] add_1_out_3, and_1_out_3, eq_1_out_3, gt_1_out_3, inv_1_out_2, lt_1_out_3, neq_1_out_3,
       noop_1_out_2, not_1_out_2, or_1_out_3, sla_1_out_2, sll_1_out_2, sra_1_out_2, srl_1_out_2,
       sub_1_out_3, zero_1_out_1;

  \not  not_1 (.A(a), .out_2(not_1_out_2));
  \and  and_1 (.A(a), .B(b), .out_3(and_1_out_3));
  \or  or_1 (.A(a), .B(b), .out_3(or_1_out_3));
  add add_1 (.A(a), .B(b), .out_3(add_1_out_3));
  sub sub_1 (.A(a), .B(b), .out_3(sub_1_out_3));
  lt lt_1 (.A(a), .B(b), .out_3(lt_1_out_3));
  gt gt_1 (.A(a), .B(b), .out_3(gt_1_out_3));
  eq eq_1 (.A(a), .B(b), .out_3(eq_1_out_3));
  neq neq_1 (.A(a), .B(b), .out_3(neq_1_out_3));
  inv inv_1 (.A(a), .out_2(inv_1_out_2));
  sll sll_1 (.A(a), .out_2(sll_1_out_2));
  srl srl_1 (.A(a), .out_2(srl_1_out_2));
  sla sla_1 (.A(a), .out_2(sla_1_out_2));
  sra sra_1 (.A(a), .out_2(sra_1_out_2));
  noop noop_1 (.A(a), .out_2(noop_1_out_2));
  zero zero_1 (.out_1(zero_1_out_1));
  Multiplexer #(.select(4), .width(17), .disabled(0)) multiplexer_1 (
    .in0(zero_1_out_1), .in1(not_1_out_2), .in2(and_1_out_3), .in3(or_1_out_3), .in4(add_1_out_3),
    .in5(sub_1_out_3), .in6(lt_1_out_3), .in7(gt_1_out_3), .in8(eq_1_out_3), .in9(neq_1_out_3),
    .in10(inv_1_out_2), .in11(sll_1_out_2), .in12(srl_1_out_2), .in13(sla_1_out_2), .in14(sra_1_out_2),
    .in15(noop_1_out_2), .out({overflow, result}), .sel(ALU_code), .en(1'b1));

  // Notes on the sheet:
  //   This circuit is used as a block in the main circuit, and its layout must remain unchanged. The circuit called "main" should be the main circuit of this file.
  //   Do not change the circuit appearance.
  //   DO NOT CHANGE THE INPUTS AND OUTPUTS OF THIS CIRCUIT!
  //   Do not add/remove inputs or outputs. Do not even change their location or orientation.
endmodule

module zero (
  output [16:0] out_1
);

  _17_bit_line__overflow u_17_bit_line_overflow_1 (.A({16{1'b0}}), .in_2(1'b0), .out_3(out_1));
endmodule

// it
module lt (
  input  [15:0] A,
  input  [15:0] B,
  output [16:0] out_3
);

  wire and_1_out, and_2_out, xnor_1_out;
  wire [0:0] or_1_out;
  wire [15:0] carry_lookahead_unit_1_s, not_1_out;

  assign not_1_out = ~B;  // NOT_Gate not_1, 16 bits wide
  carry_lookahead_unit carry_lookahead_unit_1 (
    .Carry_in(1'b1), .A(A), .B(not_1_out), .S(carry_lookahead_unit_1_s));  // open: Carry_out_overflow
  xnor xnor_1 (xnor_1_out, A[15], B[15]);
  and and_1 (and_1_out, A[15], not_1_out[15]);
  and and_2 (and_2_out, xnor_1_out, carry_lookahead_unit_1_s[15]);
  or or_1 (or_1_out[0], and_2_out, and_1_out);
  _17_bit_line__overflow u_17_bit_line_overflow_1 (.A({{15{1'b0}}, or_1_out[0]}), .in_2(1'b0), .out_3(out_3));
endmodule

module gt (
  input  [15:0] A,
  input  [15:0] B,
  output [16:0] out_3
);

  lt lt_1 (.A(B), .B(A), .out_3(out_3));
endmodule

module eq (
  input  [15:0] A,
  input  [15:0] B,
  output [16:0] out_3
);

  wire [0:0] and_1_out;
  wire [15:0] xnor_1_out;

  assign xnor_1_out = ~(A ^ B);  // XNOR_Gate xnor_1, 16 bits wide
  and and_1 (and_1_out[0], xnor_1_out[0], xnor_1_out[1], xnor_1_out[2], xnor_1_out[3], xnor_1_out[4], xnor_1_out[5], xnor_1_out[6], xnor_1_out[7], xnor_1_out[9], xnor_1_out[10], xnor_1_out[11], xnor_1_out[12], xnor_1_out[13], xnor_1_out[14], xnor_1_out[15], xnor_1_out[8]);
  _17_bit_line__overflow u_17_bit_line_overflow_1 (.A({{15{1'b0}}, and_1_out[0]}), .in_2(1'b0), .out_3(out_3));
endmodule

module \not  (
  input  [15:0] A,
  output [16:0] out_2
);

  wire [15:0] not_1_out;

  assign not_1_out = ~A;  // NOT_Gate not_1, 16 bits wide
  _17_bit_line__overflow u_17_bit_line_overflow_1 (.A(not_1_out), .in_2(1'b0), .out_3(out_2));
endmodule

module \and  (
  input  [15:0] A,
  input  [15:0] B,
  output [16:0] out_3
);

  wire [15:0] and_1_out;

  assign and_1_out = A & B;  // AND_Gate and_1, 16 bits wide
  _17_bit_line__overflow u_17_bit_line_overflow_1 (.A(and_1_out), .in_2(1'b0), .out_3(out_3));
endmodule

module \or  (
  input  [15:0] A,
  input  [15:0] B,
  output [16:0] out_3
);

  wire [15:0] or_1_out;

  assign or_1_out = A | B;  // OR_Gate or_1, 16 bits wide
  _17_bit_line__overflow u_17_bit_line_overflow_1 (.A(or_1_out), .in_2(1'b0), .out_3(out_3));
endmodule

module add (
  input  [15:0] A,
  input  [15:0] B,
  output [16:0] out_3
);

  wire carry_lookahead_unit_1_carry_out_overflow;
  wire [15:0] carry_lookahead_unit_1_s;

  carry_lookahead_unit carry_lookahead_unit_1 (
    .Carry_in(1'b0), .A(B), .B(A), .S(carry_lookahead_unit_1_s),
    .Carry_out_overflow(carry_lookahead_unit_1_carry_out_overflow));
  _17_bit_line__overflow u_17_bit_line_overflow_1 (
    .A(carry_lookahead_unit_1_s), .in_2(carry_lookahead_unit_1_carry_out_overflow), .out_3(out_3));
endmodule

module sub (
  input  [15:0] A,
  input  [15:0] B,
  output [16:0] out_3
);

  wire carry_lookahead_unit_1_carry_out_overflow;
  wire [15:0] carry_lookahead_unit_1_s, not_1_out;

  assign not_1_out = ~B;  // NOT_Gate not_1, 16 bits wide
  carry_lookahead_unit carry_lookahead_unit_1 (
    .Carry_in(1'b1), .A(not_1_out), .B(A), .S(carry_lookahead_unit_1_s),
    .Carry_out_overflow(carry_lookahead_unit_1_carry_out_overflow));
  _17_bit_line__overflow u_17_bit_line_overflow_1 (
    .A(carry_lookahead_unit_1_s), .in_2(carry_lookahead_unit_1_carry_out_overflow), .out_3(out_3));
endmodule

module neq (
  input  [15:0] A,
  input  [15:0] B,
  output [16:0] out_3
);

  wire and_1_out;
  wire [0:0] not_1_out;
  wire [15:0] xnor_1_out;

  assign xnor_1_out = ~(A ^ B);  // XNOR_Gate xnor_1, 16 bits wide
  not not_1 (not_1_out[0], and_1_out);
  and and_1 (and_1_out, xnor_1_out[0], xnor_1_out[1], xnor_1_out[2], xnor_1_out[3], xnor_1_out[4], xnor_1_out[5], xnor_1_out[6], xnor_1_out[7], xnor_1_out[9], xnor_1_out[10], xnor_1_out[11], xnor_1_out[12], xnor_1_out[13], xnor_1_out[14], xnor_1_out[15], xnor_1_out[8]);
  _17_bit_line__overflow u_17_bit_line_overflow_1 (.A({{15{1'b0}}, not_1_out[0]}), .in_2(1'b0), .out_3(out_3));
endmodule

module inv (
  input  [15:0] A,
  output [16:0] out_2
);

  sub sub_1 (.A({16{1'b0}}), .B(A), .out_3(out_2));
endmodule

module sll (
  input  [15:0] A,
  output [16:0] out_2
);

  _17_bit_line__overflow u_17_bit_line_overflow_1 (.A({A[14:0], 1'b0}), .in_2(1'b0), .out_3(out_2));
endmodule

module srl (
  input  [15:0] A,
  output [16:0] out_2
);

  _17_bit_line__overflow u_17_bit_line_overflow_1 (.A({1'b0, A[15:1]}), .in_2(1'b0), .out_3(out_2));
endmodule

module sla (
  input  [15:0] A,
  output [16:0] out_2
);

  wire xor_1_out;

  _17_bit_line__overflow u_17_bit_line_overflow_1 (.A({A[14:0], 1'b0}), .in_2(xor_1_out), .out_3(out_2));
  xor xor_1 (xor_1_out, A[14], A[15]);
endmodule

module sra (
  input  [15:0] A,
  output [16:0] out_2
);

  _17_bit_line__overflow u_17_bit_line_overflow_1 (.A({{2{A[15]}}, A[14:1]}), .in_2(1'b0), .out_3(out_2));
endmodule

module _17_bit_line__overflow (
  input  [15:0] A,
  input  in_2,
  output [16:0] out_3
);


  assign out_3 = {in_2, A};
endmodule

module noop (
  input  [15:0] A,
  output [16:0] out_2
);

  _17_bit_line__overflow u_17_bit_line_overflow_1 (.A(A), .in_2(1'b0), .out_3(out_2));
endmodule
