// Logisim project LABO2.circ as structural Verilog
module _1_Bit_Adder (
  input  A,
  input  B,
  input  C,
  output Som,
  output Carry_Out
);

  wire and_1_out, and_2_out, and_3_out, and_4_out, and_5_out, and_6_out, and_7_out, not_1_out, not_2_out,
       not_3_out, not_4_out, not_5_out, not_6_out;

  not not_1 (not_1_out, B);
  not not_2 (not_2_out, C);
  not not_3 (not_3_out, A);
  not not_4 (not_4_out, C);
  not not_5 (not_5_out, A);
  not not_6 (not_6_out, B);
  and and_1 (and_1_out, A, not_1_out, not_2_out);
  and and_2 (and_2_out, not_3_out, B, not_4_out);
  and and_3 (and_3_out, not_5_out, not_6_out, C);
  and and_4 (and_4_out, A, B, C);
  and and_5 (and_5_out, A, B);
  and and_6 (and_6_out, B, C);
  and and_7 (and_7_out, A, C);
  or or_1 (Carry_Out, and_5_out, and_6_out, and_7_out);
  or or_2 (Som, and_1_out, and_2_out, and_3_out, and_4_out);
endmodule

module _16_bit_adder_ripple_carry_adder (
  input  Pos_Neg_A,
  input  in_2,
  input  in_3,
  input  in_4,
  input  in_5,
  input  in_6,
  input  in_7,
  input  in_8,
  input  in_9,
  input  in_10,
  input  in_11,
  input  in_12,
  input  in_13,
  input  in_14,
  input  in_15,
  input  in_16,
  input  Pos___Neg_B,
  input  in_18,
  input  in_19,
  input  in_20,
  input  in_21,
  input  in_22,
  input  in_23,
  input  in_24,
  input  in_25,
  input  in_26,
  input  in_27,
  input  in_28,
  input  in_29,
  input  in_30,
  input  in_31,
  input  in_32,
  input  Carry_in,
  output Overflow,
  output out_35,
  output out_36,
  output out_37,
  output out_38,
  output out_39,
  output out_40,
  output out_41,
  output out_42,
  output out_43,
  output out_44,
  output out_45,
  output out_46,
  output out_47,
  output out_48,
  output out_49,
  output out_50,
  output [15:0] out_51
);

  wire n1_bit_adder_1_carry_out, n1_bit_adder_2_carry_out, n1_bit_adder_3_carry_out,
       n1_bit_adder_4_carry_out, n1_bit_adder_5_carry_out, n1_bit_adder_6_carry_out,
       n1_bit_adder_7_carry_out, n1_bit_adder_8_carry_out, n1_bit_adder_9_carry_out,
       n1_bit_adder_10_carry_out, n1_bit_adder_11_carry_out, n1_bit_adder_12_carry_out,
       n1_bit_adder_13_carry_out, n1_bit_adder_14_carry_out, n1_bit_adder_15_carry_out,
       n1_bit_adder_16_carry_out, xnor_1_out, xor_1_out;

  _1_Bit_Adder u_1_bit_adder_1 (
    .A(Pos_Neg_A), .B(Pos___Neg_B), .C(Carry_in), .Som(out_35), .Carry_Out(n1_bit_adder_1_carry_out));
  _1_Bit_Adder u_1_bit_adder_2 (
    .A(in_2), .B(in_18), .C(n1_bit_adder_1_carry_out), .Som(out_36), .Carry_Out(n1_bit_adder_2_carry_out));
  _1_Bit_Adder u_1_bit_adder_3 (
    .A(in_3), .B(in_19), .C(n1_bit_adder_2_carry_out), .Som(out_37), .Carry_Out(n1_bit_adder_3_carry_out));
  _1_Bit_Adder u_1_bit_adder_4 (
    .A(in_4), .B(in_20), .C(n1_bit_adder_3_carry_out), .Som(out_38), .Carry_Out(n1_bit_adder_4_carry_out));
  _1_Bit_Adder u_1_bit_adder_5 (
    .A(in_5), .B(in_21), .C(n1_bit_adder_4_carry_out), .Som(out_39), .Carry_Out(n1_bit_adder_5_carry_out));
  _1_Bit_Adder u_1_bit_adder_6 (
    .A(in_6), .B(in_22), .C(n1_bit_adder_5_carry_out), .Som(out_40), .Carry_Out(n1_bit_adder_6_carry_out));
  _1_Bit_Adder u_1_bit_adder_7 (
    .A(in_7), .B(in_23), .C(n1_bit_adder_6_carry_out), .Som(out_41), .Carry_Out(n1_bit_adder_7_carry_out));
  _1_Bit_Adder u_1_bit_adder_8 (
    .A(in_8), .B(in_24), .C(n1_bit_adder_7_carry_out), .Som(out_42), .Carry_Out(n1_bit_adder_8_carry_out));
  _1_Bit_Adder u_1_bit_adder_9 (
    .A(in_9), .B(in_25), .C(n1_bit_adder_8_carry_out), .Som(out_43), .Carry_Out(n1_bit_adder_9_carry_out));
  _1_Bit_Adder u_1_bit_adder_10 (
    .A(in_10), .B(in_26), .C(n1_bit_adder_9_carry_out), .Som(out_44), .Carry_Out(n1_bit_adder_10_carry_out));
  _1_Bit_Adder u_1_bit_adder_11 (
    .A(in_11), .B(in_27), .C(n1_bit_adder_10_carry_out), .Som(out_45), .Carry_Out(n1_bit_adder_11_carry_out));
  _1_Bit_Adder u_1_bit_adder_12 (
    .A(in_12), .B(in_28), .C(n1_bit_adder_11_carry_out), .Som(out_46), .Carry_Out(n1_bit_adder_12_carry_out));
  _1_Bit_Adder u_1_bit_adder_13 (
    .A(in_13), .B(in_29), .C(n1_bit_adder_12_carry_out), .Som(out_47), .Carry_Out(n1_bit_adder_13_carry_out));
  _1_Bit_Adder u_1_bit_adder_14 (
    .A(in_14), .B(in_30), .C(n1_bit_adder_13_carry_out), .Som(out_48), .Carry_Out(n1_bit_adder_14_carry_out));
  _1_Bit_Adder u_1_bit_adder_15 (
    .A(in_16), .B(in_32), .C(n1_bit_adder_16_carry_out), .Som(out_50), .Carry_Out(n1_bit_adder_15_carry_out));
  _1_Bit_Adder u_1_bit_adder_16 (
    .A(in_15), .B(in_31), .C(n1_bit_adder_14_carry_out), .Som(out_49), .Carry_Out(n1_bit_adder_16_carry_out));
  xnor xnor_1 (xnor_1_out, in_32, in_16);
  and and_1 (Overflow, xnor_1_out, xor_1_out);
  xor xor_1 (xor_1_out, in_16, out_50);

  assign out_51 = {out_35, out_36, out_37, out_38, out_39, out_40, out_41, out_42, out_43, out_44, out_45, out_46, out_47, out_48, out_49, out_50};
endmodule

module _4_bit_adder (
  input  A0,
  input  B0,
  input  A1,
  input  B1,
  input  A2,
  input  B2,
  input  A3,
  input  B3,
  input  C_in,
  output [3:0] S,
  output Carry_out
);

  wire carry_out_1_carry_out_1, carry_out_1_carry_out_2, carry_out_1_carry_out_3;

  carry_out carry_out_1 (
    .C0(C_in), .B3(B3), .A3(A3), .B2(B2), .A2(A2), .B1(B1), .A1(A1), .B0(B0), .A0(A0),
    .Carry_out_1(carry_out_1_carry_out_1), .Carry_out_2(carry_out_1_carry_out_2),
    .Carry_out_3(carry_out_1_carry_out_3), .Carry_out_4(Carry_out));
  _1_Bit_Adder u_1_bit_adder_1 (.A(A0), .B(B0), .C(C_in), .Som(S[0]));  // open: Carry_Out
  _1_Bit_Adder u_1_bit_adder_2 (.A(A1), .B(B1), .C(carry_out_1_carry_out_1), .Som(S[1]));  // open: Carry_Out
  _1_Bit_Adder u_1_bit_adder_3 (.A(A2), .B(B2), .C(carry_out_1_carry_out_2), .Som(S[2]));  // open: Carry_Out
  _1_Bit_Adder u_1_bit_adder_4 (.A(A3), .B(B3), .C(carry_out_1_carry_out_3), .Som(S[3]));  // open: Carry_Out
endmodule

module carry_out (
  input  C0,
  input  B3,
  input  A3,
  input  B2,
  input  A2,
  input  B1,
  input  A1,
  input  B0,
  input  A0,
  output Carry_out_1,
  output Carry_out_2,
  output Carry_out_3,
  output Carry_out_4
);

  wire and_1_out, and_2_out, and_3_out, and_4_out, and_5_out, and_6_out, and_7_out, and_8_out, and_9_out,
       and_10_out, generate_propagate_1_g, generate_propagate_1_p, generate_propagate_2_g,
       generate_propagate_2_p, generate_propagate_3_g, generate_propagate_3_p, generate_propagate_4_g,
       generate_propagate_4_p;

  Generate_propagate generate_propagate_1 (.B(B3), .A(A3), .G(generate_propagate_1_g), .P(generate_propagate_1_p));
  Generate_propagate generate_propagate_2 (.B(B2), .A(A2), .G(generate_propagate_2_g), .P(generate_propagate_2_p));
  Generate_propagate generate_propagate_3 (.B(B1), .A(A1), .G(generate_propagate_3_g), .P(generate_propagate_3_p));
  Generate_propagate generate_propagate_4 (.B(B0), .A(A0), .G(generate_propagate_4_g), .P(generate_propagate_4_p));
  and and_1 (and_1_out, generate_propagate_4_p, C0);
  and and_2 (and_2_out, generate_propagate_4_g, generate_propagate_3_p);
  and and_3 (and_3_out, generate_propagate_3_p, generate_propagate_4_p, C0);
  and and_4 (and_4_out, generate_propagate_3_g, generate_propagate_2_p);
  and and_5 (and_5_out, generate_propagate_2_p, generate_propagate_3_p, generate_propagate_4_g);
  and and_6 (and_6_out, generate_propagate_2_p, generate_propagate_3_p, generate_propagate_4_p, C0);
  and and_7 (and_7_out, generate_propagate_2_g, generate_propagate_1_p);
  and and_8 (and_8_out, generate_propagate_1_p, generate_propagate_2_p, generate_propagate_3_g);
  and and_9 (and_9_out, generate_propagate_1_p, generate_propagate_2_p, generate_propagate_3_p, generate_propagate_4_g);
  and and_10 (and_10_out, generate_propagate_1_p, generate_propagate_2_p, generate_propagate_3_p, generate_propagate_4_p, C0);
  or or_1 (Carry_out_1, generate_propagate_4_g, and_1_out);
  or or_2 (Carry_out_2, generate_propagate_3_g, and_2_out, and_3_out);
  or or_3 (Carry_out_3, generate_propagate_2_g, and_4_out, and_5_out, and_6_out);
  or or_4 (Carry_out_4, generate_propagate_1_g, and_7_out, and_8_out, and_9_out, and_10_out);
endmodule

module Generate_propagate (
  input  B,
  input  A,
  output G,
  output P
);

  and u_G (G, A, B);
  or u_P (P, A, B);
endmodule

module _16_bit_complement_carry_adder (
  input  C_in,
  input  B3,
  input  B2,
  input  B1,
  input  B0,
  input  A3,
  input  A2,
  input  A1,
  input  A0,
  output [3:0] out_10,
  output out_11
);

  _4_bit_adder u_4_bit_adder_1 (
    .C_in(C_in), .B3(B3), .A3(A3), .B2(B2), .A2(A2), .B1(B1), .A1(A1), .B0(B0), .A0(A0), .S(out_10),
    .Carry_out(out_11));
endmodule

module carry_lookahead_unit (
  input  [15:0] A,
  input  [15:0] B,
  input  Carry_in,
  output Carry_out_overflow,
  output [15:0] S
);

  wire n4_bit_adder_1_carry_out, n4_bit_adder_2_carry_out, n4_bit_adder_3_carry_out, xnor_1_out, xor_1_out;

  _4_bit_adder u_4_bit_adder_1 (
    .C_in(Carry_in), .B3(A[3]), .A3(B[3]), .B2(A[2]), .A2(B[2]), .B1(A[1]), .A1(B[1]), .B0(A[0]), .A0(B[0]),
    .S(S[3:0]), .Carry_out(n4_bit_adder_1_carry_out));
  _4_bit_adder u_4_bit_adder_2 (
    .C_in(n4_bit_adder_1_carry_out), .B3(B[7]), .A3(A[7]), .B2(B[6]), .A2(A[6]), .B1(B[5]), .A1(A[5]),
    .B0(B[4]), .A0(A[4]), .S(S[7:4]), .Carry_out(n4_bit_adder_2_carry_out));
  _4_bit_adder u_4_bit_adder_3 (
    .C_in(n4_bit_adder_2_carry_out), .B3(B[11]), .A3(A[11]), .B2(B[10]), .A2(A[10]), .B1(B[9]), .A1(A[9]),
    .B0(B[8]), .A0(A[8]), .S(S[11:8]), .Carry_out(n4_bit_adder_3_carry_out));
  _4_bit_adder u_4_bit_adder_4 (
    .C_in(n4_bit_adder_3_carry_out), .B3(B[15]), .A3(A[15]), .B2(B[14]), .A2(A[14]), .B1(B[13]), .A1(A[13]),
    .B0(B[12]), .A0(A[12]), .S(S[15:12]));  // open: Carry_out
  xnor xnor_1 (xnor_1_out, B[15], A[15]);
  xor xor_1 (xor_1_out, A[15], S[15]);
  and and_1 (Carry_out_overflow, xnor_1_out, xor_1_out);
endmodule
