// Logisim project SD_GroupXX.circ as structural Verilog: 9 circuits, main circuit main
module main (
  input  in_1,
  output [15:0] pc,
  output [15:0] r0,
  output [15:0] r1,
  output [15:0] r2,
  output [15:0] r3,
  output [15:0] r4,
  output [15:0] r5,
  output [15:0] r6,
  output [15:0] r7,
  output [15:0] r8,
  output [15:0] r9,
  output [15:0] r10,
  output [15:0] r11,
  output [15:0] r12,
  output [15:0] r13,
  output [15:0] r14,
  output [15:0] r15,
  output [15:0] out_19,
  output halt
);

  wire and_1_out, clock_1_out, LW, not_1_out, not_2_out, R2_SRC, reset_out, SW, unary_1_out_2;
  wire [3:0] memadd_1_nopc, multiplexer_1_out, multiplexer_3_out, split_1_operartion_code_instruction_code,
       split_1_operation_code___rt, split_1_rd, split_1_rs;
  wire [15:0] multiplexer_4_out, n16_bit_alu_1_result, ram_1_data, ram_2_data, register_file_1_s,
       register_file_1_t, Sign_ext_out_2;

  Halt halt_1 (.instruction(ram_1_data), .clock(clock_1_out), .reset(reset_out), .halt(halt));
  Clock clock_1 (.out(clock_1_out));
  Button reset (.out(reset_out));
  and and_1 (and_1_out, ~halt, clock_1_out);  // AND_Gate
  PC pc_1 (.R(reset_out), .C(and_1_out), .BA(1'b0), .BR(1'b0), .BV({16{1'b1}}), .\output (pc));
  RAM #(.addrWidth(16), .dataWidth(16), .bus("separate")) ram_1 (
    .addr(pc), .data(ram_1_data), .str(in_1));  // open: din, sel, clk, ld, clr
  split split_1 (
    .in_1(ram_1_data), .Operation_code___rt(split_1_operation_code___rt), .rd(split_1_rd), .rs(split_1_rs),
    .operartion_code_instruction_code(split_1_operartion_code_instruction_code));
  control control_1 (.in_1(split_1_operartion_code_instruction_code), .SW(SW), .LW(LW), .R2_SRC(R2_SRC));
  sign_ext Sign_ext (.in_1(split_1_operation_code___rt), .out_2(Sign_ext_out_2));
  Multiplexer #(.width(4), .disabled(0), .enable("false")) multiplexer_1 (
    .in0(split_1_operation_code___rt), .in1(split_1_rs), .out(multiplexer_1_out), .sel(SW));
  not not_1 (not_1_out, SW);
  register_file register_file_1 (
    .DATA(multiplexer_4_out), .rd(split_1_rs), .Write(not_1_out), .R(reset_out), .rs(split_1_rd),
    .rt(multiplexer_1_out), .C(and_1_out), .S(register_file_1_s), .T(register_file_1_t), .G0(r0), .G1(r1),
    .G2(r2), .G3(r3), .G4(r4), .G5(r5), .G6(r6), .G7(r7), .G8(r8), .G9(r9), .G10(r10), .G11(r11), .G12(r12),
    .G13(r13), .G14(r14), .G15(r15));
  unary unary_1 (.in_1(split_1_operartion_code_instruction_code), .out_2(unary_1_out_2));
  memAdd memadd_1 (.OPC(split_1_operartion_code_instruction_code), .SW(SW), .LW(LW), .NOPC(memadd_1_nopc));
  Multiplexer #(.width(16), .disabled(0)) multiplexer_2 (
    .in0(register_file_1_t), .in1(Sign_ext_out_2), .out(out_19), .sel(R2_SRC), .en(and_1_out));
  Multiplexer #(.width(4), .disabled(0)) multiplexer_3 (
    .in0(memadd_1_nopc), .in1(split_1_operation_code___rt), .out(multiplexer_3_out), .sel(unary_1_out_2),
    .en(and_1_out));
  _16_bit_ALU u_16_bit_alu_1 (
    .ALU_code(multiplexer_3_out), .a(register_file_1_s), .b(out_19), .result(n16_bit_alu_1_result));  // open: overflow
  not not_2 (not_2_out, and_1_out);
  RAM #(.addrWidth(16), .dataWidth(16), .bus("separate")) ram_2 (
    .addr(n16_bit_alu_1_result), .din(register_file_1_t), .data(ram_2_data), .str(SW), .sel(1'b1),
    .clk(not_2_out));  // open: ld, clr
  Multiplexer #(.width(16), .disabled(0)) multiplexer_4 (
    .in0(n16_bit_alu_1_result), .in1(ram_2_data), .out(multiplexer_4_out), .sel(LW), .en(and_1_out));

  // Notes on the sheet:
  //   current instruction
  //   clock signal
  //   reset button
  //   DO NOT CHANGE THE INPUTS AND OUTPUTS OF THIS CIRCUIT! Do not add/remove inputs or outputs. Do not even change their location or orientation.
endmodule

module Halt (
  input  [15:0] instruction,
  input  clock,
  input  reset,
  output halt
);

  wire and_1_out, comparator_1_eq, comparator_2_gt, counter_1_carry, or_1_out, or_2_out;
  wire [11:0] counter_1_q;

  Comparator #(.width(16), .mode("unsigned")) comparator_1 (
    .a(instruction), .b({16{1'b0}}), .eq(comparator_1_eq));  // open: gt, lt
  Counter #(.width(12), .max('hfff), .trigger("falling")) counter_1 (
    .Q(counter_1_q), .carry(counter_1_carry), .clk(clock), .clr(reset));  // open: load, D, count
  or or_1 (or_1_out, comparator_1_eq, counter_1_carry);
  Comparator #(.width(12), .mode("unsigned")) comparator_2 (
    .a(counter_1_q), .b({12{1'b0}}), .gt(comparator_2_gt));  // open: eq, lt
  or or_2 (or_2_out, halt, and_1_out);
  and and_1 (and_1_out, or_1_out, comparator_2_gt);
  Register #(.width(1)) register_1 (.D(or_2_out), .Q(halt), .clk(clock), .clr(reset));  // open: en

  // Notes on the sheet:
  //   halt becomes and stays asserted if the instruction is 0000 (not in the first clock cycle) or the end of the counter is reached (2^12)
endmodule

module PC (
  input  R,
  input  C,
  input  BA,
  input  BR,
  input  [15:0] BV,
  output [15:0] \output 
);

  wire add_one_1_add_by_bv, add_one_1_add_one, add_one_1_normal_input, or_1_out;
  wire [15:0] carry_lookahead_unit_1_s, carry_lookahead_unit_2_s, multiplexer_1_out, multiplexer_2_out,
       multiplexer_3_out, multiplexer_4_out;

  or or_1 (or_1_out, R, C);
  carry_lookahead_unit carry_lookahead_unit_1 (
    .Carry_in(1'b0), .A(BV), .B(\output ), .S(carry_lookahead_unit_1_s));  // open: Carry_out_overflow
  add_one add_one_1 (
    .BA(BA), .BR(BR), .add_one(add_one_1_add_one), .normal_input(add_one_1_normal_input),
    .add_by_BV(add_one_1_add_by_bv));
  Multiplexer #(.width(16)) multiplexer_1 (
    .in0(BV), .in1(carry_lookahead_unit_1_s), .out(multiplexer_1_out), .sel(add_one_1_add_by_bv),
    .en(or_1_out));
  Multiplexer #(.width(16)) multiplexer_2 (
    .in0(multiplexer_1_out), .in1(\output ), .out(multiplexer_2_out), .sel(add_one_1_normal_input),
    .en(or_1_out));
  carry_lookahead_unit carry_lookahead_unit_2 (
    .Carry_in(1'b0), .A(16'h1), .B(multiplexer_2_out), .S(carry_lookahead_unit_2_s));  // open: Carry_out_overflow
  Multiplexer #(.width(16)) multiplexer_3 (
    .in0(multiplexer_2_out), .in1(carry_lookahead_unit_2_s), .out(multiplexer_3_out),
    .sel(add_one_1_add_one), .en(or_1_out));
  Multiplexer #(.width(16)) multiplexer_4 (
    .in0(multiplexer_3_out), .in1({16{1'b0}}), .out(multiplexer_4_out), .sel(R), .en(or_1_out));
  _16_bit_register u_16_bit_register_1 (
    .D(multiplexer_4_out), .C(or_1_out), .write(1'b1), .Q(\output ));  // open: reset
endmodule

module add_one (
  input  BA,
  input  BR,
  output add_one,
  output normal_input,
  output add_by_BV
);

  wire not_2_out;

  not not_1 (add_one, BA);
  and and_1 (normal_input, add_one, not_2_out);
  not not_2 (not_2_out, BR);

  assign add_by_BV = BR;
endmodule

module split (
  input  [15:0] in_1,
  output [3:0] Operation_code___rt,
  output [3:0] rd,
  output [3:0] rs,
  output [3:0] operartion_code_instruction_code
);


  assign operartion_code_instruction_code = in_1[15:12];
  assign Operation_code___rt = in_1[3:0];
  assign rd = in_1[7:4];
  assign rs = in_1[11:8];
endmodule

module unary (
  input  [3:0] in_1,
  output out_2
);

  wire not_1_out, not_2_out, not_3_out;

  not not_1 (not_1_out, in_1[1]);
  not not_2 (not_2_out, in_1[2]);
  not not_3 (not_3_out, in_1[3]);
  and and_1 (out_2, in_1[0], not_1_out, not_2_out, not_3_out);
endmodule

module control (
  input  [3:0] in_1,
  output SW,
  output LW,
  output R2_SRC
);

  wire not_1_out, not_2_out, not_3_out;

  not not_1 (not_1_out, in_1[2]);
  not not_2 (not_2_out, in_1[0]);
  not not_3 (not_3_out, in_1[2]);
  and and_1 (SW, in_1[0], in_1[1], not_1_out, in_1[3]);
  and and_2 (LW, not_2_out, in_1[1], not_3_out, in_1[3]);
  or or_1 (R2_SRC, SW, LW);
endmodule

module sign_ext (
  input  [3:0] in_1,
  output [15:0] out_2
);


  assign out_2 = {{13{in_1[3]}}, in_1[2:0]};
endmodule

module memAdd (
  input  [3:0] OPC,
  input  SW,
  input  LW,
  output [3:0] NOPC
);

  wire or_1_out;

  Multiplexer #(.width(4), .disabled(0), .enable("false")) multiplexer_1 (
    .in0(OPC), .in1(4'b0100), .out(NOPC), .sel(or_1_out));
  or or_1 (or_1_out, SW, LW);
endmodule
