// Logisim project counter.circ as structural Verilog
module Counter (
  input  C,
  input  [15:0] D,
  output [15:0] \output 
);

  wire comparator_1_eq, comparator_1_gt, or_1_out;
  wire [15:0] carry_lookahead_unit_1_s;

  carry_lookahead_unit carry_lookahead_unit_1 (
    .Carry_in(1'b0), .A(16'h1), .B(\output ), .S(carry_lookahead_unit_1_s));  // open: Carry_out_overflow
  _16_bit_register u_16_bit_register_1 (
    .D(carry_lookahead_unit_1_s), .C(C), .write(1'b1), .reset(or_1_out), .Q(\output ));
  Comparator #(.width(16), .mode("unsigned")) comparator_1 (
    .a(\output ), .b(D), .gt(comparator_1_gt), .eq(comparator_1_eq));  // open: lt
  or or_1 (or_1_out, comparator_1_gt, comparator_1_eq);
endmodule
