// Logisim project finite-state machine.circ as structural Verilog: 1 circuit, main circuit main
module main (
  output [15:0] out_1,
  output [15:0] out_2
);

  wire clock_1_out, comparator_1_eq, comparator_2_eq, comparator_3_eq, comparator_4_eq, comparator_5_eq,
       comparator_6_eq, d_ff_1_q, d_ff_2_q, d_ff_3_q, d_ff_4_q, d_ff_5_q, d_ff_6_q;

  Clock clock_1 (.out(clock_1_out));
  Counter counter_1 (.C(clock_1_out), .D(16'h1c), .\output (out_1));
  Comparator #(.width(16), .mode("unsigned")) comparator_1 (
    .a(out_1), .b(16'hc), .eq(comparator_1_eq));  // open: gt, lt
  Comparator #(.width(16), .mode("unsigned")) comparator_2 (
    .a(out_1), .b(16'h8), .eq(comparator_2_eq));  // open: gt, lt
  Comparator #(.width(16), .mode("unsigned")) comparator_3 (
    .a(out_1), .b({16{1'b0}}), .eq(comparator_3_eq));  // open: gt, lt
  Comparator #(.width(16), .mode("unsigned")) comparator_4 (
    .a(out_1), .b(16'h1a), .eq(comparator_4_eq));  // open: gt, lt
  Comparator #(.width(16), .mode("unsigned")) comparator_5 (
    .a(out_1), .b(16'h16), .eq(comparator_5_eq));  // open: gt, lt
  Comparator #(.width(16), .mode("unsigned")) comparator_6 (
    .a(out_1), .b(16'he), .eq(comparator_6_eq));  // open: gt, lt
  D_Flip_Flop d_ff_1 (
    .clk(comparator_1_eq), .D(comparator_1_eq), .Q(d_ff_1_q), .reset(d_ff_3_q));  // open: Qn, preset, en
  D_Flip_Flop d_ff_2 (
    .clk(comparator_2_eq), .D(comparator_2_eq), .Q(d_ff_2_q), .reset(d_ff_1_q));  // open: Qn, preset, en
  D_Flip_Flop d_ff_3 (
    .clk(comparator_3_eq), .D(comparator_3_eq), .Q(d_ff_3_q), .reset(d_ff_2_q));  // open: Qn, preset, en
  D_Flip_Flop d_ff_4 (
    .clk(comparator_4_eq), .D(comparator_4_eq), .Q(d_ff_4_q), .reset(d_ff_6_q));  // open: Qn, preset, en
  D_Flip_Flop d_ff_5 (
    .clk(comparator_5_eq), .D(comparator_5_eq), .Q(d_ff_5_q), .reset(d_ff_4_q));  // open: Qn, preset, en
  D_Flip_Flop d_ff_6 (
    .clk(comparator_6_eq), .D(comparator_6_eq), .Q(d_ff_6_q), .reset(d_ff_5_q));  // open: Qn, preset, en
  LED led_1 (.in(d_ff_1_q));
  LED led_2 (.in(d_ff_2_q));
  LED led_3 (.in(d_ff_3_q));
  LED led_4 (.in(d_ff_4_q));
  LED led_5 (.in(d_ff_5_q));
  LED led_6 (.in(d_ff_6_q));

  assign out_2 = 16'he;
endmodule
